# Fritzing sketch Fritzing File (saved by Fritzing 0.9.4)
circuit board: 8.47cm x 5.64444cm

parts:
  Part2 = Adafruit Analog 2-Axis Joystick [part_number="Adafruit #512"]
  LED1 = LED - 5mm [color="Red (633nm)" package="5 mm [THT]"]
  LED2 = LED - 5mm [color="Red (633nm)" package="5 mm [THT]"]
  LED3 = LED - 5mm [color="Red (633nm)" package="5 mm [THT]"]
  Part1 = Arduino Uno (Rev3)
  Part3 = Adafruit Thermocouple Amplifier MAX31855 [part_number="Adafruit #269"]

nets:
  GND: Part2.GND, LED1.anode, LED3.anode, Part1.GND, Part3.GND
  N1: Part2.SWITCH, Part1.D2
  N2: Part2.YOUT, Part1.A1
  N3: Part2.XOUT, Part1.A0
  VCC: Part2.VCC, LED3.cathode, Part1.5V, Part3.VIN
  N4: LED1.cathode, Part1.D13/SCK
  N5: LED2.cathode, Part1.A4/SDA
  N6: LED2.anode, Part1.A5/SCL
  N7: Part1.D3_PWM, Part3.DO
  N8: Part1.D4, Part3.CS
  N9: Part1.D5_PWM, Part3.CLK

notes:
  LEDs Represent Pins to I2C LCD
  LED Represent Pins to Heater and Fan Relay
  GND
  SEL
  Y OUT
  X OUT
  VCC
  VIN
  CLK
  CS
  DO
  SCL
  Relay

custom parts:
  Adafruit Analog 2-Axis Joystick: This mini-kit makes it easy to mount a PSP/Xbox-like thumb joystick to your project. The thumbstick is an analog joystick - more accurate and sensitive than just 'directional' joysticks - with a 'press in to select' button. Since it's analog, you'll need two analog reading pins on your microcontroller to determine X and Y. Having an extra digital input will let you read the switch. The pack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
  Adafruit Thermocouple Amplifier MAX31855: Thermocouples are very sensitive, requiring a good amplifier with a cold-compensation reference. The MAX31855K does everything for you, and can be easily interfaced with any microcontroller, even one without an analog input. This breakout board has the chip itself, a 3.3V regulator with 10uF bypass capacitors and level shifting circuitry, all assembled and tested. Comes with a 2 pin terminal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
